// Logisim project SAP1.circ as structural Verilog: 3 circuits, main circuit main
module main (
  output [7:0] out_1
);

  wire clock_1_out;

  Clock clock_1 (.out(clock_1_out));
  ProgramCounter programcounter_1 (.Ep(1'b1), .Cp(1'b0), .CLK_(clock_1_out), .PC(out_1));  // open: CLR_INV
  MAR mar_1 (.WBus(out_1), .Lm(1'b1), .CLK(clock_1_out), .CE_(1'b0), .out_5(out_1));
endmodule

module ProgramCounter (
  input  Ep,
  input  Cp,
  input  CLK_,
  input  CLR_INV,
  output [7:0] PC
);

  wire not_1_out, not_2_out, not_3_out, not_4_out;
  wire [7:0] c74LS126_q;

  not not_1 (not_1_out, CLK_);
  J_K_Flip_Flop c74LS126 (.J(1'b1), .K(1'b1), .clk(not_1_out), .Q(c74LS126_q[0]), .reset(CLR_INV));  // open: Qn, preset
  not not_2 (not_2_out, c74LS126_q[0]);
  J_K_Flip_Flop j_k_ff_1 (.J(1'b1), .K(1'b1), .clk(not_2_out), .Q(c74LS126_q[1]), .reset(CLR_INV));  // open: Qn, preset
  not not_3 (not_3_out, c74LS126_q[1]);
  J_K_Flip_Flop j_k_ff_2 (.J(1'b1), .K(1'b1), .clk(not_3_out), .Q(c74LS126_q[2]), .reset(CLR_INV));  // open: Qn, preset
  not not_4 (not_4_out, c74LS126_q[2]);
  J_K_Flip_Flop j_k_ff_3 (.J(1'b1), .K(1'b1), .clk(not_4_out), .Q(c74LS126_q[3]), .reset(CLR_INV));  // open: Qn, preset
  assign PC = Ep ? c74LS126_q : 8'bz;  // Controlled_Buffer controlled_buffer_1
endmodule

module MAR (
  input  [7:0] WBus,
  input  Lm,
  input  CLK,
  input  CE_,
  output [7:0] out_5
);

  wire multiplexer_1_out, not_1_out, RUN_PROG_sw2, WRITE_sw1;
  wire [3:0] ADDRESS_sw4, c74LS173_q, controlled_buffer_1_out, multiplexer_2_out;
  wire [7:0] DATA_sw8, ram_1_dout;

  // Probe on controlled_buffer_1_out
  assign controlled_buffer_1_out = Lm ? WBus[3:0] : 4'bz;  // Controlled_Buffer controlled_buffer_1
  DipSwitch #(.number(4)) ADDRESS (
    .sw1(ADDRESS_sw4[3]), .sw2(ADDRESS_sw4[2]), .sw3(ADDRESS_sw4[1]), .sw4(ADDRESS_sw4[0]));
  Register #(.width(4)) c74LS173 (.D(controlled_buffer_1_out), .en(1'b1), .clk(CLK), .Q(c74LS173_q), .clr(1'b0));
  DipSwitch #(.number(2)) RUN_PROG (.sw2(RUN_PROG_sw2));  // open: sw1
  // Probe on multiplexer_2_out
  Multiplexer #(.enable("false")) multiplexer_1 (.in0(1'b0), .in1(CE_), .out(multiplexer_1_out), .sel(RUN_PROG_sw2));
  Multiplexer #(.width(4), .enable("false")) multiplexer_2 (
    .in0(ADDRESS_sw4), .in1(c74LS173_q), .out(multiplexer_2_out), .sel(multiplexer_1_out));
  DipSwitch #(.number(2)) WRITE (.sw1(WRITE_sw1));  // open: sw2
  DipSwitch DATA (
    .sw1(DATA_sw8[7]), .sw2(DATA_sw8[6]), .sw3(DATA_sw8[5]), .sw4(DATA_sw8[4]), .sw5(DATA_sw8[3]),
    .sw6(DATA_sw8[2]), .sw7(DATA_sw8[1]), .sw8(DATA_sw8[0]));
  RAM #(.addrWidth(4), .databus("bibus")) ram_1 (
    .addr(multiplexer_2_out), .we(WRITE_sw1), .oe(1'b1), .clk(CLK), .din(DATA_sw8), .dout(ram_1_dout));
  not not_1 (not_1_out, multiplexer_1_out);
  assign out_5 = not_1_out ? ram_1_dout : 8'bz;  // Controlled_Buffer controlled_buffer_2
endmodule
